# Fritzing sketch WebSocketSensor (saved by Fritzing 0.9.2b)
breadboards: 1

parts:
  Squix1 = OLED 0.96" 128x64 I2C SSD1306
  U1 = NodeMCU V1.0
  AM1 = AM2320 Humidity and Temperature Sensor [part_number="Adafruit #3721"]

nets:
  VCC: Squix1.VCC, U1.3V3, AM1.VDD
  GND: Squix1.GND, U1.GND, AM1.GND

notes:
  Red = 3.3V
  Black = Gnd
  Yellow = SDA
  Blue = SCL
  D1 = GPIO5 (SCL)
  D2 = GPIO4 (SDA)
  SD2 = GPIO9 (SDA)
  SD3 = GPIO10 (SCL)

custom parts:
  NodeMCU V1.0: ESP8266 based NodeMCU
  AM2320 Humidity and Temperature Sensor: AM2320 I2C Humidity and Temperature Sensor
